// Logisim project shifterCircuitLogisim.circ as structural Verilog: 1 circuit, main circuit main
module main (
  input  a15,
  input  a14,
  input  a13,
  input  a12,
  input  a11,
  input  a10,
  input  a9,
  input  a8,
  input  a7,
  input  a6,
  input  a5,
  input  a4,
  input  a3,
  input  a2,
  input  a1,
  input  a0,
  input  Selector,
  output overflow,
  output out15,
  output out14,
  output out13,
  output out12,
  output out11,
  output out10,
  output out9,
  output out8,
  output out7,
  output out6,
  output out5,
  output out4,
  output out3,
  output out2,
  output out1,
  output out0
);

  wire and_2_out, and_3_out, and_5_out, and_6_out, and_7_out, and_8_out, and_9_out, and_10_out, and_11_out,
       and_12_out, and_13_out, and_14_out, and_15_out, and_16_out, and_17_out, and_18_out, and_19_out,
       and_20_out, and_21_out, and_22_out, and_23_out, and_24_out, and_25_out, and_26_out, and_27_out,
       and_28_out, and_29_out, and_31_out, not_1_out;

  not not_1 (not_1_out, Selector);
  and and_1 (overflow, not_1_out, not_1_out, a15);
  and and_2 (and_2_out, a15, Selector);
  and and_3 (and_3_out, a14, Selector);
  and and_4 (out15, not_1_out, a14);
  or or_1 (out14, and_2_out, and_5_out);
  and and_5 (and_5_out, not_1_out, a13);
  and and_6 (and_6_out, a13, Selector);
  or or_2 (out13, and_3_out, and_7_out);
  and and_7 (and_7_out, not_1_out, a12);
  and and_8 (and_8_out, a12, Selector);
  or or_3 (out12, and_6_out, and_9_out);
  and and_9 (and_9_out, not_1_out, a11);
  or or_4 (out11, and_8_out, and_11_out);
  and and_10 (and_10_out, a11, Selector);
  and and_11 (and_11_out, not_1_out, a10);
  and and_12 (and_12_out, a10, Selector);
  or or_5 (out10, and_10_out, and_13_out);
  and and_13 (and_13_out, not_1_out, a9);
  and and_14 (and_14_out, a9, Selector);
  or or_6 (out9, and_12_out, and_15_out);
  and and_15 (and_15_out, not_1_out, a8);
  and and_16 (and_16_out, a8, Selector);
  or or_7 (out8, and_14_out, and_17_out);
  and and_17 (and_17_out, not_1_out, a7);
  or or_8 (out7, and_16_out, and_19_out);
  and and_18 (and_18_out, a7, Selector);
  and and_19 (and_19_out, not_1_out, a6);
  and and_20 (and_20_out, a6, Selector);
  or or_9 (out6, and_18_out, and_21_out);
  and and_21 (and_21_out, not_1_out, a5);
  and and_22 (and_22_out, a5, Selector);
  or or_10 (out5, and_20_out, and_23_out);
  and and_23 (and_23_out, not_1_out, a4);
  and and_24 (and_24_out, a4, Selector);
  or or_11 (out4, and_22_out, and_25_out);
  and and_25 (and_25_out, not_1_out, a3);
  or or_12 (out3, and_24_out, and_27_out);
  and and_26 (and_26_out, a3, Selector);
  and and_27 (and_27_out, not_1_out, a2);
  and and_28 (and_28_out, a2, Selector);
  or or_13 (out2, and_26_out, and_29_out);
  and and_29 (and_29_out, not_1_out, a1);
  and and_30 (out0, a1, Selector);
  or or_14 (out1, and_28_out, and_31_out);
  and and_31 (and_31_out, not_1_out, a0);
endmodule
